# Fritzing sketch PhysicalSketch (saved by Fritzing 0.9.2b)
perfboards: 1

parts:
  Composant2 = Arduino Nano (Rev3.0)
  Rx1 = mystery part, 4 pins [chip_label=Sensor]
  Tx2 = mystery part, 3 pins [chip_label=Tilt]
  R1 = Resistor [tolerance=±5% resistance=220 package=THT]
  S1 = Toggle Switch [package=THT]
  VCC1 = 4 x AAA Battery Mount
  U1 = LCD-16X2 [package=lcd-16x2]
  Tx1 = mystery part, 3 pins [chip_label=Emitter]
  LED1 = smd LED [color="Red (633nm)" package="1206 [SMD]"]

nets:
  N1: Composant2.GND, Rx1.pin4, VCC1.-, U1.K
  N2: Composant2.D2, Rx1.pin3
  N3: Composant2.D4, Tx2.pin3
  N4: Composant2.D5, U1.DB7
  N5: Composant2.D6, U1.DB6
  N6: Composant2.D7, U1.DB5
  N7: Composant2.D8, U1.DB4
  N8: Composant2.D9, U1.E, U1.DB0
  N9: Composant2.D10, U1.RS
  N10: Composant2.D11/MOSI, Tx1.pin3
  N11: Composant2.VIN, S1.L1
  N12: Composant2.5V, Tx2.pin2
  N13: Composant2.3V3, U1.A
  N14: Rx1.pin1, U1.VDD
  N15: Tx2.pin1, U1.VSS, U1.VO, U1.R_W, Tx1.pin1
  N16: R1.Pin_1, LED1.anode
  N17: S1.L2, VCC1.+
