# Fritzing sketch Sketch (saved by Fritzing 0.9.2b)

parts:
  Composant2 = Arduino Nano (Rev3.0)
  U1 = LCD-16X2 [package=lcd-16x2_noholes]
  LED1 = smd LED [color="Red (633nm)" package="1206 [SMD]"]  # not connected
  Tx1 = mystery part, 3 pins [chip_label=?]
  Rx1 = mystery part, 4 pins [chip_label=?]
  J1 = Power Jack [package=power_jack_combo]
  Tx2 = mystery part, 3 pins [chip_label=?]
  R1 = Resistor [tolerance=±5% resistance=220 package="2010 [SMD]"]
  R2 = Resistor [tolerance=±5% resistance=220 package="2010 [SMD]"]

nets:
  GND: Composant2.GND, J1.GND
  N1: Composant2.D2, Rx1.pin3
  N2: Composant2.D3, Tx1.pin1
  N3: Composant2.D4, U1.RS
  N4: Composant2.D5, U1.E
  N5: Composant2.D6, U1.DB4
  N6: Composant2.D7, U1.DB5
  N7: Composant2.D8, U1.DB6
  N8: Composant2.D9, U1.DB7
  N9: Composant2.D10, Tx2.pin1
  N10: Composant2.D11/MOSI, R1.Pin_0
  N11: Composant2.VIN, J1.PWR
  VSS: U1.VSS, U1.VDD
  N12: U1.A, R2.Pin_1

notes:
  RF 433
  Emitter
  RF 433
  Receiver
  Tilt switch
